# Fritzing sketch zenith (saved by Fritzing 1.0.1rc)
breadboards: 1

parts:
  ESP32-S3_N8R2 = ESP32-S3-DevKitC-1-N8R8-v1 [part_number=ESP32-S3-DevKitC-1-N8R8-v1]
  IC1 = Stereo 3.7W Class D Amplifier [mn="Maxim Integrated" mpn=MAX98357BETE+ package=16-TQFN]
  BIGTREETECH_TMC2209_V1_1 = TMC2209
  A1 = DFR Sen0539-EN
  SP1 = SPEAKER [package=pcb_mount_speaker]
  Tuner_Encoder = Rotary Encoder [package=THT]
  Volume_Encoder = Rotary Encoder [package=THT]
  SP2 = SPEAKER [package=pcb_mount_speaker]
  M2 = RioRand LM2596
  M3 = Stepper Motor - Bipolar
  1k_resistor = Resistor [tolerance=±5% resistance=220 package="1206 [SMD]"]
  Home_Reed_SW = SWITCH-MOMENTARY-2 [package=reed_switch_pth]
  RED_LED = smd LED [color="Red (633nm)" package="0805 [SMD]"]
  GRN_LED = smd LED [color="Red (633nm)" package="0805 [SMD]"]
  100k_resistor = Resistor [tolerance=±5% resistance=220 package="1206 [SMD]"]
  R1 = Resistor [tolerance=±5% resistance=220 package="0402 [SMD]"]
  R2 = Resistor [tolerance=±5% resistance=220 package="0402 [SMD]"]

nets:
  N1: ESP32-S3_N8R2.pin_2, BIGTREETECH_TMC2209_V1_1.VDD
  N2: ESP32-S3_N8R2.pin_4, Volume_Encoder.SwitchrPinD
  N3: ESP32-S3_N8R2.pin_5, BIGTREETECH_TMC2209_V1_1.STEP
  N4: ESP32-S3_N8R2.pin_6, BIGTREETECH_TMC2209_V1_1.DIRECTION
  N5: ESP32-S3_N8R2.pin_7, IC1.LRCLK
  N6: ESP32-S3_N8R2.pin_9, BIGTREETECH_TMC2209_V1_1.ENABLE
  N7: ESP32-S3_N8R2.pin_10, 1k_resistor.Pin_1
  N8: ESP32-S3_N8R2.pin_11, BIGTREETECH_TMC2209_V1_1.PDN1
  N9: ESP32-S3_N8R2.pin_12, A1.Pin_1
  N10: ESP32-S3_N8R2.pin_15, A1.Pin_2
  N11: ESP32-S3_N8R2.pin_16, Tuner_Encoder.EncoderPinB
  N12: ESP32-S3_N8R2.pin_17, Volume_Encoder.EncoderPinB
  N13: ESP32-S3_N8R2.pin_18, Volume_Encoder.EncoderPinA
  N14: ESP32-S3_N8R2.pin_19, Tuner_Encoder.EncoderPinA
  N15: ESP32-S3_N8R2.pin_20, Tuner_Encoder.SwitchrPinD
  N16: ESP32-S3_N8R2.pin_22, ESP32-S3_N8R2.pin_23, ESP32-S3_N8R2.pin_24, ESP32-S3_N8R2.pin_44, BIGTREETECH_TMC2209_V1_1.GROUND_MT, BIGTREETECH_TMC2209_V1_1.GROUND_LOG, A1.Pin_3, M2.Pin_4, Home_Reed_SW.2
  N17: ESP32-S3_N8R2.pin_27, IC1.DIN
  N18: ESP32-S3_N8R2.pin_37, R2.Pin_0
  N19: ESP32-S3_N8R2.pin_38, R1.Pin_0
  N20: ESP32-S3_N8R2.pin_40, IC1.BCLK
  N21: ESP32-S3_N8R2.pin_41, Home_Reed_SW.1
  N22: IC1.GAIN__SLOT, 100k_resistor.Pin_1
  GND: IC1.GND, Tuner_Encoder.EncoderPinC, Tuner_Encoder.SwitchPinE, Volume_Encoder.EncoderPinC, Volume_Encoder.SwitchPinE, RED_LED.cathode, GRN_LED.cathode, 100k_resistor.Pin_0
  N23: IC1.VDD, BIGTREETECH_TMC2209_V1_1.VM, A1.Pin_4, M2.Pin_3
  N24: IC1.OUTP, SP2.-
  N25: IC1.OUTN, SP2.+
  N26: BIGTREETECH_TMC2209_V1_1.OUT_B2, M3.A
  N27: BIGTREETECH_TMC2209_V1_1.OUT_A2, M3.D
  N28: BIGTREETECH_TMC2209_V1_1.OUT_A1, M3.B
  N29: BIGTREETECH_TMC2209_V1_1.OUT_B1, M3.C
  N30: A1.Pin_5, SP1.-
  N31: A1.Pin_6, SP1.+
  N32: RED_LED.anode, R1.Pin_1
  N33: GRN_LED.anode, R2.Pin_1

custom parts:
  ESP32-S3-DevKitC-1-N8R8-v1: ESP32-S3-DevKitC-1-N8R8-v1 This module is 44pins long (2x22) and 11 pins width.
  Stereo 3.7W Class D Amplifier: Mono 3.2W Class D Amplifier Datasheet: https://datasheets.maximintegrated.com/en/ds/MAX98357A-MAX98357B.pdf The MAX98357B is an easy-to-use, low-cost, digital pulse-code modulation (PCM) input Class D amplifier that provides industry-leading Class AB audio performance with Class D efficiency. The digital audio interface automatically recognizes up to 35 different PCM and TDM clocking schemes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
  TMC2209: This is a Stepper Motor Controller for integrated circuits.
  DFR Sen0539-EN: Offline Language Learning Voice Recognition Sensor.
  Rotary Encoder: Rotary Encoder from ALPSec11e with switch. This version has an alternate (which has been used in boards) pcb footprint from @opera_night in the forums. It is probably the best one to start from to see if you part matches.
